// Logisim project cpu.circ as structural Verilog: 1 circuit, main circuit cpu
module cpu (
  input  clk,
  input  [31:0] Instruction,
  input  [31:0] MemReadData,
  output [31:0] MemAddress,
  output [31:0] ProgramCounter,
  output [31:0] ra,
  output [31:0] sp,
  output [31:0] t0,
  output [31:0] t1,
  output [31:0] t2,
  output [31:0] s0,
  output [31:0] s1,
  output [31:0] a0,
  output [3:0] MemWriteMask,
  output [31:0] MemWriteData
);

  wire ASel, BrEq, BrLt, BrUn, BSel, MemWEn, PCSel, RegWEn;
  wire [1:0] WBSel;
  wire [2:0] funct3, ImmSel;
  wire [3:0] ALUSel;
  wire [6:0] func7;
  wire [24:0] Inst_pipe;
  wire [31:0] A, adder_1_out, adder_2_out, B, DataToReg, imm, inst_flush, pc, PC_pipe, read_data1,
       read_data2, RegWriteData;

  Adder #(.width(32)) adder_1 (.a(ProgramCounter), .b(32'h4), .out(adder_1_out));  // open: cin, cout
  Register #(.width(32)) u_PC (.D(pc), .clk(clk), .Q(ProgramCounter));  // open: en, clr
  Multiplexer #(.width(32)) multiplexer_1 (.in0(adder_1_out), .in1(MemAddress), .out(pc), .sel(PCSel));
  Multiplexer #(.width(32)) multiplexer_2 (.in0(Instruction), .in1(32'h13), .out(inst_flush), .sel(PCSel));
  Register #(.width(32)) register_1 (.D(ProgramCounter), .clk(clk), .Q(PC_pipe));  // open: en, clr
  Register #(.width(32)) register_2 (
    .D(inst_flush), .clk(clk), .Q({func7, Inst_pipe[24:15], funct3, Inst_pipe[11:0]}));  // open: en, clr
  regfile regfile_1 (
    .ReadIndex1(Inst_pipe[19:15]), .ReadIndex2(Inst_pipe[24:20]), .WriteIndex(Inst_pipe[11:7]),
    .WriteData(RegWriteData), .RegWEn(RegWEn), .clk(clk), .ra(ra), .sp(sp), .t0(t0), .t1(t1), .t2(t2),
    .s0(s0), .s1(s1), .a0(a0), .ReadData1(read_data1), .ReadData2(read_data2));
  imm_gen imm_gen_1 (
    .Instruction({func7, Inst_pipe[24:15], funct3, Inst_pipe[11:0]}), .ImmSel(ImmSel), .Immediate(imm));
  control_logic control_logic_1 (
    .Instruction({func7, Inst_pipe[24:15], funct3, Inst_pipe[11:0]}), .BrEq(BrEq), .BrLt(BrLt),
    .PCSel(PCSel), .RegWEn(RegWEn), .ImmSel(ImmSel), .BrUn(BrUn), .ASel(ASel), .BSel(BSel), .ALUSel(ALUSel),
    .MemWEn(MemWEn), .WBSel(WBSel));
  Multiplexer #(.width(32)) multiplexer_3 (.in0(read_data1), .in1(PC_pipe), .out(A), .sel(ASel));
  Multiplexer #(.width(32)) multiplexer_4 (.in0(read_data2), .in1(imm), .out(B), .sel(BSel));
  alu alu_1 (.A(A), .B(B), .ALUSel(ALUSel), .ALUResult(MemAddress));
  branch_comp branch_comp_1 (.BrData1(read_data1), .BrData2(read_data2), .BrUn(BrUn), .BrEq(BrEq), .BrLt(BrLt));
  Adder #(.width(32)) adder_2 (.a(PC_pipe), .b(32'h4), .out(adder_2_out));  // open: cin, cout
  partial_store partial_store_1 (
    .Instruction({func7, Inst_pipe[24:15], funct3, Inst_pipe[11:0]}), .MemAddress(MemAddress),
    .DataFromReg(read_data2), .MemWEn(MemWEn), .MemWriteMask(MemWriteMask), .DataToMem(MemWriteData));
  partial_load partial_load_1 (
    .Instruction({func7, Inst_pipe[24:15], funct3, Inst_pipe[11:0]}), .MemAddress(MemAddress),
    .DataFromMem(MemReadData), .DataToReg(DataToReg));
  Multiplexer #(.select(2), .width(32)) multiplexer_5 (
    .in0(DataToReg), .in1(MemAddress), .in2(adder_2_out), .out(RegWriteData), .sel(WBSel));  // open: in3

  // Other names for the same wires on the sheet: ALUResult[31:0] = MemAddress;
  //   Inst_pipe (some bits) = {func7, funct3}; opcode[6:0] = Inst_pipe[6:0]; rd[4:0] = Inst_pipe[11:7];
  //   rs1[4:0] = Inst_pipe[19:15]; rs2[4:0] = Inst_pipe[24:20]

  // Notes on the sheet:
  //   To IMEM
  //   IMEM (do **NOT** move this)
  //   From IMEM
  //   Inputs/Outputs for testing. Do **NOT** move these.
  //   It is OK to move the PC, RegFile, ALU, MEM, Branch Comp, Imm Gen, Partial Load, Partial Store and Control Logic to wherever is most convenient for you when constructing your CPU, and to delete this text
  //   To DMEM
  //   DMEM (do **NOT** move this)
  //   From DMEM
endmodule
