// Logisim project partial-load.circ as structural Verilog: 1 circuit, main circuit partial_load
module partial_load (
  input  [31:0] Instruction,
  input  [31:0] MemAddress,
  input  [31:0] DataFromMem,
  output [31:0] DataToReg
);

  wire comparator_1_eq;
  wire [31:0] lb, lb00, lb01, lb10, lb11, lh, lh00, lh01, lh10;

  assign lb01 = {{24{DataFromMem[15]}}, DataFromMem[15:8]};  // Bit_Extender bit_extender_1
  assign lb10 = {{24{DataFromMem[23]}}, DataFromMem[23:16]};  // Bit_Extender bit_extender_2
  assign lb11 = {{24{DataFromMem[31]}}, DataFromMem[31:24]};  // Bit_Extender bit_extender_3
  assign lh10 = {{16{DataFromMem[31]}}, DataFromMem[31:16]};  // Bit_Extender bit_extender_4
  assign lb00 = {{24{DataFromMem[7]}}, DataFromMem[7:0]};  // Bit_Extender bit_extender_5
  assign lh00 = {{16{DataFromMem[15]}}, DataFromMem[15:0]};  // Bit_Extender bit_extender_6
  assign lh01 = {{16{DataFromMem[23]}}, DataFromMem[23:8]};  // Bit_Extender bit_extender_7
  Multiplexer #(.select(3), .width(32)) multiplexer_1 (
    .in0(lb), .in1(lh), .in2(DataFromMem), .out(DataToReg), .sel(Instruction[14:12]));  // open: in3, in4, in5, in6, in7
  Comparator #(.width(7)) comparator_1 (.a(Instruction[6:0]), .b(7'b0000011), .eq(comparator_1_eq));  // open: gt, lt
  Multiplexer #(.select(2), .width(32)) multiplexer_2 (
    .in0(lh00), .in1(lh01), .in2(lh10), .out(lh), .sel(MemAddress[1:0]));  // open: in3
  Multiplexer #(.select(2), .width(32)) multiplexer_3 (
    .in0(lb00), .in1(lb01), .in2(lb10), .in3(lb11), .out(lb), .sel(MemAddress[1:0]));

  // Other names for the same wires on the sheet: lw[31:0] = DataFromMem; func7[6:0] = Instruction[31:25];
  //   funct3[2:0] = Instruction[14:12]; bottom2bits[1:0] = MemAddress[1:0]; opcode[6:0] = Instruction[6:0];
  //   rd[4:0] = Instruction[11:7]; rs1[4:0] = Instruction[19:15]; rs2[4:0] = Instruction[24:20]

  // Notes on the sheet:
  //   INPUTS to your circuit
  //   DON'T CHANGE THE LOCATIONS OF THE INPUTS AND OUTPUTS!
  //   OUTPUT from your circuit
endmodule
