// Logisim project partial-store.circ as structural Verilog: 1 circuit, main circuit partial_store
module partial_store (
  input  [31:0] Instruction,
  input  [31:0] MemAddress,
  input  [31:0] DataFromReg,
  input  MemWEn,
  output [3:0] MemWriteMask,
  output [31:0] DataToMem
);

  wire [3:0] bit_extender_1_out, mask_SB, mask_SH, multiplexer_4_out;
  wire [31:0] sb, sh;

  Multiplexer #(.select(2), .width(32)) multiplexer_1 (
    .in0({{24{1'b0}}, DataFromReg[7:0]}), .in1({{16{1'b0}}, DataFromReg[7:0], {8{1'b0}}}),
    .in2({{8{1'b0}}, DataFromReg[7:0], {16{1'b0}}}), .in3({DataFromReg[7:0], {24{1'b0}}}), .out(sb),
    .sel(MemAddress[1:0]));
  Multiplexer #(.select(2), .width(32)) multiplexer_2 (
    .in0({{16{1'b0}}, DataFromReg[15:0]}), .in2({DataFromReg[15:0], {16{1'b0}}}), .out(sh),
    .sel(MemAddress[1:0]));  // open: in1, in3
  Multiplexer #(.select(3), .width(32)) multiplexer_3 (
    .in0(sb), .in1(sh), .in2(DataFromReg), .out(DataToMem), .sel(Instruction[14:12]));  // open: in3, in4, in5, in6, in7
  Multiplexer #(.select(3), .width(4)) multiplexer_4 (
    .in0(mask_SB), .in1(mask_SH), .in2(4'b1111), .out(multiplexer_4_out), .sel(Instruction[14:12]));  // open: in3, in4, in5, in6, in7
  assign bit_extender_1_out = {{3{MemWEn}}, MemWEn};  // Bit_Extender bit_extender_1
  assign MemWriteMask = multiplexer_4_out & bit_extender_1_out;  // AND_Gate and_1, 4 bits wide
  Multiplexer #(.select(2), .width(4)) multiplexer_5 (
    .in0(4'b0001), .in1(4'b0010), .in2(4'b0100), .in3(4'b1000), .out(mask_SB), .sel(MemAddress[1:0]));
  Multiplexer #(.select(2), .width(4)) multiplexer_6 (
    .in0(4'b0011), .in2(4'b1100), .out(mask_SH), .sel(MemAddress[1:0]));  // open: in1, in3

  // Other names for the same wires on the sheet: func7[6:0] = Instruction[31:25]; funct3[2:0] = Instruction[14:12];
  //   bottom2bits[1:0] = MemAddress[1:0]; opcode[6:0] = Instruction[6:0]; rd[4:0] = Instruction[11:7];
  //   rs1[4:0] = Instruction[19:15]; rs2[4:0] = Instruction[24:20]; dataSB[7:0] = DataFromReg[7:0];
  //   dataSH[15:0] = DataFromReg[15:0]; sb7_0[7:0] = DataFromReg[7:0]; sb15_8[15:8] = DataFromReg[7:0];
  //   sb16_23[23:16] = DataFromReg[7:0]; sb24_31[31:24] = DataFromReg[7:0]; sh15_0[15:0] = DataFromReg[15:0];
  //   sh31_16[31:16] = DataFromReg[15:0]; sw[31:0] = DataFromReg

  // Notes on the sheet:
  //   INPUTS to your circuit
  //   DON'T CHANGE THE LOCATIONS OF THE INPUTS AND OUTPUTS!
  //   OUTPUT from your circuit
endmodule
