// Logisim project regfile.circ as structural Verilog: 1 circuit, main circuit regfile
// x4
module regfile (
  input  [4:0] ReadIndex1,
  input  [4:0] ReadIndex2,
  input  [4:0] WriteIndex,
  input  [31:0] WriteData,
  input  RegWEn,
  input  clk,
  output [31:0] ra,
  output [31:0] sp,
  output [31:0] t0,
  output [31:0] t1,
  output [31:0] t2,
  output [31:0] s0,
  output [31:0] s1,
  output [31:0] a0,
  output [31:0] ReadData1,
  output [31:0] ReadData2
);

  wire reg0, reg1, reg2, reg3, reg4, reg5, reg6, reg7, reg8, reg9, reg10, reg11, reg12, reg13, reg14, reg15,
       reg16, reg17, reg18, reg19, reg20, reg21, reg22, reg23, reg24, reg25, reg26, reg27, reg28, reg29,
       reg30, reg31;
  wire [31:0] x3, x4, x11, x12, x13, x14, x15, x16, x17, x18, x19, x20, x21, x22, x23, x24, x25, x26, x27,
       x28, x29, x30, x31;

  Register #(.width(32)) x1 (.D(WriteData), .en(reg1), .clk(clk), .Q(ra));  // open: clr
  Register #(.width(32)) x2 (.D(WriteData), .en(reg2), .clk(clk), .Q(sp));  // open: clr
  Register #(.width(32)) u_x3 (.D(WriteData), .en(reg3), .clk(clk), .Q(x3));  // open: clr
  Register #(.width(32)) u_x4 (.D(WriteData), .en(reg4), .clk(clk), .Q(x4));  // open: clr
  Register #(.width(32)) x5 (.D(WriteData), .en(reg5), .clk(clk), .Q(t0));  // open: clr
  Register #(.width(32)) x6 (.D(WriteData), .en(reg6), .clk(clk), .Q(t1));  // open: clr
  Register #(.width(32)) x7 (.D(WriteData), .en(reg7), .clk(clk), .Q(t2));  // open: clr
  Register #(.width(32)) x8 (.D(WriteData), .en(reg8), .clk(clk), .Q(s0));  // open: clr
  Demultiplexer #(.select(5)) demultiplexer_1 (
    .out0(reg0), .out1(reg1), .out2(reg2), .out3(reg3), .out4(reg4), .out5(reg5), .out6(reg6), .out7(reg7),
    .out8(reg8), .out9(reg9), .out10(reg10), .out11(reg11), .out12(reg12), .out13(reg13), .out14(reg14),
    .out15(reg15), .out16(reg16), .out17(reg17), .out18(reg18), .out19(reg19), .out20(reg20), .out21(reg21),
    .out22(reg22), .out23(reg23), .out24(reg24), .out25(reg25), .out26(reg26), .out27(reg27), .out28(reg28),
    .out29(reg29), .out30(reg30), .out31(reg31), .in(RegWEn), .sel(WriteIndex));
  Register #(.width(32)) x9 (.D(WriteData), .en(reg9), .clk(clk), .Q(s1));  // open: clr
  Register #(.width(32)) x10 (.D(WriteData), .en(reg10), .clk(clk), .Q(a0));  // open: clr
  Register #(.width(32)) u_x11 (.D(WriteData), .en(reg11), .clk(clk), .Q(x11));  // open: clr
  Register #(.width(32)) u_x12 (.D(WriteData), .en(reg12), .clk(clk), .Q(x12));  // open: clr
  Register #(.width(32)) u_x13 (.D(WriteData), .en(reg13), .clk(clk), .Q(x13));  // open: clr
  Register #(.width(32)) u_x14 (.D(WriteData), .en(reg14), .clk(clk), .Q(x14));  // open: clr
  Register #(.width(32)) u_x15 (.D(WriteData), .en(reg15), .clk(clk), .Q(x15));  // open: clr
  Register #(.width(32)) u_x16 (.D(WriteData), .en(reg16), .clk(clk), .Q(x16));  // open: clr
  Register #(.width(32)) u_x17 (.D(WriteData), .en(reg17), .clk(clk), .Q(x17));  // open: clr
  Register #(.width(32)) u_x18 (.D(WriteData), .en(reg18), .clk(clk), .Q(x18));  // open: clr
  Register #(.width(32)) u_x19 (.D(WriteData), .en(reg19), .clk(clk), .Q(x19));  // open: clr
  Register #(.width(32)) u_x20 (.D(WriteData), .en(reg20), .clk(clk), .Q(x20));  // open: clr
  Register #(.width(32)) u_x21 (.D(WriteData), .en(reg21), .clk(clk), .Q(x21));  // open: clr
  Register #(.width(32)) u_x22 (.D(WriteData), .en(reg22), .clk(clk), .Q(x22));  // open: clr
  Register #(.width(32)) u_x23 (.D(WriteData), .en(reg23), .clk(clk), .Q(x23));  // open: clr
  Register #(.width(32)) u_x24 (.D(WriteData), .en(reg24), .clk(clk), .Q(x24));  // open: clr
  Register #(.width(32)) u_x25 (.D(WriteData), .en(reg25), .clk(clk), .Q(x25));  // open: clr
  Register #(.width(32)) u_x26 (.D(WriteData), .en(reg26), .clk(clk), .Q(x26));  // open: clr
  Register #(.width(32)) u_x27 (.D(WriteData), .en(reg27), .clk(clk), .Q(x27));  // open: clr
  Register #(.width(32)) u_x28 (.D(WriteData), .en(reg28), .clk(clk), .Q(x28));  // open: clr
  Register #(.width(32)) u_x29 (.D(WriteData), .en(reg29), .clk(clk), .Q(x29));  // open: clr
  Register #(.width(32)) u_x30 (.D(WriteData), .en(reg30), .clk(clk), .Q(x30));  // open: clr
  Register #(.width(32)) u_x31 (.D(WriteData), .en(reg31), .clk(clk), .Q(x31));  // open: clr
  Multiplexer #(.select(5), .width(32)) multiplexer_1 (
    .in0({32{1'b0}}), .in1(ra), .in2(sp), .in3(x3), .in4(x4), .in5(t0), .in6(t1), .in7(t2), .in8(s0),
    .in9(s1), .in10(a0), .in11(x11), .in12(x12), .in13(x13), .in14(x14), .in15(x15), .in16(x16), .in17(x17),
    .in18(x18), .in19(x19), .in20(x20), .in21(x21), .in22(x22), .in23(x23), .in24(x24), .in25(x25),
    .in26(x26), .in27(x27), .in28(x28), .in29(x29), .in30(x30), .in31(x31), .out(ReadData1), .sel(ReadIndex1));
  Multiplexer #(.select(5), .width(32)) multiplexer_2 (
    .in0({32{1'b0}}), .in1(ra), .in2(sp), .in3(x3), .in4(x4), .in5(t0), .in6(t1), .in7(t2), .in8(s0),
    .in9(s1), .in10(a0), .in11(x11), .in12(x12), .in13(x13), .in14(x14), .in15(x15), .in16(x16), .in17(x17),
    .in18(x18), .in19(x19), .in20(x20), .in21(x21), .in22(x22), .in23(x23), .in24(x24), .in25(x25),
    .in26(x26), .in27(x27), .in28(x28), .in29(x29), .in30(x30), .in31(x31), .out(ReadData2), .sel(ReadIndex2));

  // Other names for the same wires on the sheet: x1[31:0] = ra; x2[31:0] = sp; x5[31:0] = t0; x6[31:0] = t1;
  //   x7[31:0] = t2; x8[31:0] = s0; x9[31:0] = s1; x10[31:0] = a0

  // Notes on the sheet:
  //   INPUTS to your circuit
  //   DON'T CHANGE THE LOCATIONS OF THE INPUTS AND OUTPUTS!
  //   These are DEBUG/TEST outputs from your circuit.
  //   OUTPUTS from your circuit
endmodule
