// Logisim project ex4.circ as structural Verilog: 1 circuit, main circuit pipelined
module pipelined (
  input  [7:0] in1,
  input  [7:0] in2,
  input  CLK,
  output [7:0] out1
);

  wire [7:0] adder_1_out, multiplier_1_out, register_1_q;

  Multiplier multiplier_1 (.a(in1), .b(in2), .out(multiplier_1_out));  // open: cin, cout
  Register register_1 (.D(multiplier_1_out), .clk(CLK), .Q(register_1_q));  // open: en, clr
  Register register_2 (.D(adder_1_out), .clk(CLK), .Q(out1));  // open: en, clr
  Adder adder_1 (.a(register_1_q), .b(out1), .out(adder_1_out));  // open: cin, cout

  // Other names for the same wires on the sheet: A[7:0] = in1; B[7:0] = in2; clock = CLK
endmodule
